# Fritzing sketch diagram (saved by Fritzing 0.9.2b)
breadboards: 1

parts:
  Motor_Shield = Arduino Motor Shield (Rev3)
  Motor = Stepper Motor - Bipolar
  R1 = Rotary Potentiometer (Large) [maximum_resistance=100kΩ package=THT]
  Power_12V_2amp = Power plug

nets:
  N1: Motor_Shield.GND, R1.leg1
  N2: Motor_Shield.5V, R1.leg2
  N3: Motor_Shield.A1, R1.wiper
  N4: Motor_Shield.B-, Motor.D
  N5: Motor_Shield.B+, Motor.B
  N6: Motor_Shield.A-, Motor.C
  N7: Motor_Shield.A+, Motor.A
  N8: Motor_Shield.VMOT, Power_12V_2amp.GND
  VIN: Motor_Shield.VIN, Power_12V_2amp.VCC
